# Fritzing sketch Robotic Hand (saved by Fritzing 1.0.5)
breadboards: 1

parts:
  J1 = Basic Servo
  J2 = Basic Servo
  J3 = Basic Servo
  J4 = Basic Servo
  J5 = Basic Servo
  Part1 = Arduino Uno (Rev3)
  Part2 = Bluetooth HC-05 Macho
  C1 = Electrolytic Capacitor [capacitance=10µF voltage=16V package="100 mil [THT, electrolytic]"]
  JACK1 = 2.1mm Barrel Jack with Terminal Block
  X1 = USB Connectors [package=usb-a-s]

nets:
  N1: J1.pulse, Part1.D3_PWM
  N2: J2.pulse, Part1.D4
  N3: J3.pulse, Part1.D5_PWM
  N4: J4.pulse, Part1.D2
  GND: J5.gnd, Part1.GND, Part2.GND, C1.-, JACK1.NEG, X1.GND
  VCC: J5.vcc, Part1.5V, Part2.VCC, C1.+, JACK1.POS, X1.VBUS
  N5: J5.pulse, Part1.D7
  N6: Part1.D10_PWM/SS, Part2.TXD
  N7: Part1.D11_PWM/MOSI, Part2.RXD

notes:
  USB Connection to Arduino as Ouput
  Thumb
  Index
  Ring
  Middle
  Pinky
  5V 4 A Input
  16 V 1000UF
